# Fritzing sketch CH32V003-Thermometer (saved by Fritzing 1.0.6)
breadboards: 1
perfboards: 1

parts:
  S2 = Momentary Switch 6mm 2pin
  S3 = 0.91 inch OLED I2C Display 128 x 32 Pixels
  DS1 = DS18B20 1-Wire Temperature Sensor [part_number=DS18B20]

nets:
  GND: S2.2, S3.GND, DS1.GND
  VCC: S3.VCC, DS1.VDD

notes:
  温度センサー素子
  OLED モジュール
  CH32V003 開発ボード
  ブレッドボード 170H
  タクトスイッチ
  USB 端子が右側になるように取り付ける
  平らな面が正面を向くように取り付ける

custom parts:
  Momentary Switch 6mm 2pin: Momentary Switch 6mm 2 pin Button commonly used for reset or general input.
